// Logisim project proutiti.circ as structural Verilog: 3 circuits, main circuit main
module main (
  input  [7:0] B,
  input  [7:0] A,
  output [3:0] P
);

  wire A0B1_out, A0B2_out, A0B3_out, A1B0_out, A1B1_out, A1B2_out, A2B0_out, A2B1_out, A3B0_out, fuadd_1_res,
       fuadd_1_s, fuadd_2_res, fuadd_2_s, haadd_1_r, haadd_2_r, haadd_3_r, haadd_3_s, rest_res;

  and A0B0 (P[0], B[0], A[0]);
  and A0B1 (A0B1_out, B[1], A[0]);
  and A1B0 (A1B0_out, B[0], A[1]);
  and A0B2 (A0B2_out, B[0], B[2]);
  and A1B1 (A1B1_out, A[1], B[1]);
  and A2B0 (A2B0_out, A[2], B[0]);
  and A0B3 (A0B3_out, A[0], B[3]);
  and A1B2 (A1B2_out, A[1], B[2]);
  and A2B1 (A2B1_out, A[2], B[1]);
  and A3B0 (A3B0_out, A[3], B[0]);
  HaAdd haadd_1 (.A(A0B1_out), .B(A1B0_out), .S(P[1]), .R(haadd_1_r));
  FuAdd fuadd_1 (.R(haadd_1_r), .A(A0B2_out), .B(A1B1_out), .S(fuadd_1_s), .Res(fuadd_1_res));
  FuAdd fuadd_2 (.R(rest_res), .A(A0B3_out), .B(A1B2_out), .S(fuadd_2_s), .Res(fuadd_2_res));
  HaAdd haadd_2 (.A(fuadd_2_res), .B(haadd_3_r), .R(haadd_2_r));  // open: S
  HaAdd haadd_3 (.A(A2B1_out), .B(A3B0_out), .S(haadd_3_s), .R(haadd_3_r));
  FuAdd rest (.R(fuadd_1_res), .A(fuadd_1_s), .B(A2B0_out), .S(P[2]), .Res(rest_res));
  FuAdd fuadd_3 (.R(haadd_2_r), .A(fuadd_2_s), .B(haadd_3_s), .S(P[3]));  // open: Res
endmodule

module HaAdd (
  input  A,
  input  B,
  output S,
  output R
);

  xor xor_1 (S, A, B);
  and and_1 (R, A, B);
endmodule

module FuAdd (
  input  R,
  input  A,
  input  B,
  output S,
  output Res
);

  wire haadd_1_r, haadd_1_s, haadd_2_r;

  HaAdd haadd_1 (.A(B), .B(R), .S(haadd_1_s), .R(haadd_1_r));
  HaAdd haadd_2 (.A(A), .B(haadd_1_s), .S(S), .R(haadd_2_r));
  or or_1 (Res, haadd_2_r, haadd_1_r);
endmodule
